# Fritzing sketch atayalPatternEMFSensing (saved by Fritzing 0.8.7b)

parts:
  U2 = attiny85 [package=dip]
  Part1 = LilyPad Coin Cell Battery Holder
  R1 = Resistor [tolerance=±5% resistance=10M package=THT]
  TRS1 = Audio Jack (TRS) 3.5mm [package="4Ucon 08780 [THT]"]

nets:
  N1: U2.Pin_3, R1.Pin_0
  N2: U2.Pin_4, Part1.-, R1.Pin_1
  N3: U2.Pin_5, TRS1.Ring
  N4: U2.Pin_8, Part1.+
