# Fritzing sketch AtayalSoundToColorMountain (saved by Fritzing 0.8.7b)
perfboards: 1

parts:
  U1 = LIPO-110mAh [package=lipo-110]
  MIC1 = MAX4466 Electret Microphone Breakout Board
  U2 = attiny85 [package=dip]
  RGB_SMD_LED1 = SMD RGB LED (WS2812) [package=5050]
  RGB_SMD_LED2 = SMD RGB LED (WS2812) [package=5050]
  RGB_SMD_LED3 = SMD RGB LED (WS2812) [package=5050]
  RGB_SMD_LED4 = SMD RGB LED (WS2812) [package=5050]
  S2 = Toggle Switch [package=THT]

nets:
  VCC: U1.+, MIC1.VCC, U2.Pin_8, RGB_SMD_LED4.VCC
  N1: U1.-, S2.COM
  N2: MIC1.out, U2.Pin_3
  N3: MIC1.GND, U2.Pin_4, RGB_SMD_LED4.DOut, S2.L1
  N4: U2.Pin_6, RGB_SMD_LED4.DIn
  N5: RGB_SMD_LED1.DOut, RGB_SMD_LED2.VSS
  N6: RGB_SMD_LED1.DIn, RGB_SMD_LED2.VDD
  N7: RGB_SMD_LED1.VCC, RGB_SMD_LED2.NC
  N8: RGB_SMD_LED2.DOut, RGB_SMD_LED3.VSS
  N9: RGB_SMD_LED2.DIn, RGB_SMD_LED3.VDD
  N10: RGB_SMD_LED2.VCC, RGB_SMD_LED3.NC
  N11: RGB_SMD_LED3.DOut, RGB_SMD_LED4.VSS
  N12: RGB_SMD_LED3.DIn, RGB_SMD_LED4.VDD
  N13: RGB_SMD_LED3.VCC, RGB_SMD_LED4.NC

custom parts:
  MAX4466 Electret Microphone Breakout Board: MAX4466 Electrec Microphone Breakout Board
